// Logisim project Lab2_ZheningZhang_ChenChen_Finalized.circ as structural Verilog
module Main (
  input  in_1,
  input  in_2,
  output [31:0] out_3,
  output [31:0] out_4,
  output [31:0] out_5,
  output [31:0] out_6,
  output [31:0] out_7,
  output [31:0] out_8,
  output [31:0] out_9,
  output [31:0] out_10,
  output [31:0] out_11,
  output [31:0] out_12
);

  wire and_1_out, CLK, combjal_1_jal, combstr_1_str, goBEQ, isBEQ, isEqual, isj_jal_1_true, isjr_1_true,
       MuxSE, or_1_out, WrReg;
  wire [1:0] combwrdata_1_w1, pcmuxctr_1_ctr0;
  wire [3:0] aluctrr_1_c0, ijaluctr_1_c0, multiplexer_5_out;
  wire [4:0] multiplexer_2_out, Rd, Rs, Rt, WrAddr;
  wire [5:0] func, op;
  wire [10:6] rom_1_data;
  wire [31:0] n26to32labelextention_1_out_2, RamDataOut, SEimmeS2, WrData;

  Multiplexer #(.select(2), .width(32), .enable("false")) multiplexer_1 (
    .in0(out_4), .in1(out_4), .in2(out_10), .in3(out_7), .out(out_5), .sel(pcmuxctr_1_ctr0));
  PC pc_1 (
    .PC_Addr(out_3), .CLOCK(CLK), .PC_RESET(in_1), .Add_Sub_Ctrl(in_2), .NEXT_PC_Addr(out_4),
    .PCInput(out_5), .BEQOprand(SEimmeS2), .BEQ(goBEQ));  // open: PC_PAUSE, Carry_Out
  isBEQ isbeq_1 (.op5(op[5]), .op4(op[4]), .op3(op[3]), .op2(op[2]), .op1(op[1]), .op0(op[0]), .true(isBEQ));
  isJR isjr_1 (
    .func5(func[5]), .func4(func[4]), .func3(func[3]), .func2(func[2]), .func1(func[1]), .func0(func[0]),
    .true(isjr_1_true));
  isJ_JAL isj_jal_1 (
    .op5(op[5]), .op4(op[4]), .op3(op[3]), .op2(op[2]), .op1(op[1]), .op0(op[0]), .true(isj_jal_1_true));
  Multiplexer #(.width(5), .enable("false")) multiplexer_2 (
    .in0(Rt), .in1({5{1'b1}}), .out(multiplexer_2_out), .sel(combjal_1_jal));
  Register_File register_file_1 (
    .WrAddr(WrAddr), .WrData(WrData), .WrReg(WrReg), .RdAddr1(Rt), .RdAddr2(Rs), .RdData1(out_8),
    .RdData2(out_7), .Clock(CLK));
  and and_1 (and_1_out, MuxSE, isjr_1_true);
  isEqual isequal_1 (.in_1(out_12), .out_2(isEqual));
  CombJAL combjal_1 (.op5(op[5]), .op4(op[4]), .op3(op[3]), .op2(op[2]), .op1(op[1]), .op0(op[0]), .JAL(combjal_1_jal));
  Multiplexer #(.width(5), .enable("false")) multiplexer_3 (
    .in0(multiplexer_2_out), .in1(Rd), .out(WrAddr), .sel(MuxSE));
  and and_2 (goBEQ, isEqual, isBEQ);
  ROM #(.dataWidth(32)) rom_1 (.addr(out_3[9:2]), .data({op, Rs, Rt, Rd, rom_1_data, func}));  // open: sel
  pCMuxCtr pcmuxctr_1 (
    .isBEQ(isBEQ), .isJR(and_1_out), .isJJAL(isj_jal_1_true), .isEqual(isEqual), .ctr1(pcmuxctr_1_ctr0[1]),
    .ctr0(pcmuxctr_1_ctr0[0]));
  Clock clock_1 (.out(CLK));
  CombStr combstr_1 (.op5(op[5]), .op4(op[4]), .op3(op[3]), .op2(op[2]), .op1(op[1]), .op0(op[0]), .str(combstr_1_str));
  // Probe on {Rd, rom_1_data, func}
  _32shif2 u_32shif2_1 (.in_1(out_11), .out_2(SEimmeS2));
  _16to32SignExtention u_16to32signextention_1 (.in_1({Rd, rom_1_data, func}), .out_2(out_11));
  // Probe on out_11
  // Probe on SEimmeS2
  _26to32labelExtention u_26to32labelextention_1 (
    .in_1({Rs, Rt, Rd, rom_1_data, func}), .out_2(n26to32labelextention_1_out_2));
  CombWrReg combwrreg_1 (.op5(op[5]), .op4(op[4]), .op3(op[3]), .op2(op[2]), .op1(op[1]), .op0(op[0]), .RegW(WrReg));
  RAM #(.dataWidth(32), .bus("separate")) ram_1 (
    .addr(out_12[7:0]), .din(out_8), .data(RamDataOut), .str(combstr_1_str), .clk(CLK), .ld(1'b1));  // open: sel, clr
  MUXsel muxsel_1 (.op5(op[5]), .op4(op[4]), .op3(op[3]), .op2(op[2]), .op1(op[1]), .op0(op[0]), .MuxS(MuxSE));
  _32shif2 u_32shif2_2 (.in_1(n26to32labelextention_1_out_2), .out_2(out_10));
  or or_1 (or_1_out, MuxSE, isBEQ);
  CombWrData combwrdata_1 (
    .op5(op[5]), .op4(op[4]), .op3(op[3]), .op2(op[2]), .op1(op[1]), .op0(op[0]), .W1(combwrdata_1_w1[0]),
    .W2(combwrdata_1_w1[1]));
  isEqual isequal_2 (.in_1(out_12), .out_2(isEqual));
  IJALUCtr ijaluctr_1 (
    .op5(op[5]), .op4(op[4]), .op3(op[3]), .op2(op[2]), .op1(op[1]), .op0(op[0]), .c3(ijaluctr_1_c0[3]),
    .c2(ijaluctr_1_c0[2]), .c1(ijaluctr_1_c0[1]), .c0(ijaluctr_1_c0[0]));
  ALUCtrR aluctrr_1 (
    .f5(func[5]), .f4(func[4]), .f3(func[3]), .c3(aluctrr_1_c0[3]), .f2(func[2]), .f1(func[1]), .f0(func[0]),
    .c2(aluctrr_1_c0[2]), .c1(aluctrr_1_c0[1]), .c0(aluctrr_1_c0[0]));
  Multiplexer #(.width(32), .enable("false")) multiplexer_4 (.in0(out_11), .in1(out_8), .out(out_6), .sel(or_1_out));
  // Probe on combwrdata_1_w1
  // Probe on RamDataOut
  Multiplexer #(.width(4), .enable("false")) multiplexer_5 (
    .in0(ijaluctr_1_c0), .in1(aluctrr_1_c0), .out(multiplexer_5_out), .sel(MuxSE));
  ALU alu_1 (.ALUCtl(multiplexer_5_out), .A(out_7), .B(out_6), .ALUResult(out_12));  // open: Zero, Overflow, Shamt
  Multiplexer #(.select(2), .width(32), .enable("false")) multiplexer_6 (
    .in0(out_12), .in2(RamDataOut), .in3(out_4), .out(WrData), .sel(combwrdata_1_w1));  // open: in1
  // Probe on out_4
  // Probe on WrData
  // Probe on out_3
  // Probe on nothing
  // Probe on nothing
  // Probe on nothing
  // Probe on nothing
  // Probe on nothing
  // Probe on nothing
  // Probe on nothing
  // Probe on nothing
  // Probe on nothing

  assign out_9 = out_7;

  // Other names for the same wires on the sheet: _26SE[31:0] = out_10; NextPC[31:0] = out_4; PC[31:0] = out_3;
  //   ALUResult[31:0] = out_12; RamAddress[31:0] = out_12; RsD[31:0] = out_7; RamDataIn[31:0] = out_8;
  //   RtD[31:0] = out_8; SEimme[31:0] = out_11

  // Notes on the sheet:
  //   I type
  //   R type
  //   contents of rom_1 (hex, n*v repeats v):
  //   20010008 34220005 3043ffff 612020 832822 223024 c33826 aca40064 8ca80064 22482a 1265025 214bfff6
  //   10b602b c00000f 200d0001 23ff0018 10c00003 a13022 8000010 200e0001 3e00008 200f0001 20100001
  //   I type
  //   R type
  //   J type
  //   I type
  //   R type
endmodule

module _32_Bit_Adder_Subtractor (
  input  Add_Sub_control,
  input  [31:0] in_2,
  input  [31:0] in_3,
  output [31:0] out_4,
  output carry_out
);

  wire adder_1_cout, subtractor_1_bout;
  wire [31:0] adder_1_out, subtractor_1_out;

  Adder #(.width(32)) adder_1 (.a(in_2), .b(in_3), .out(adder_1_out), .cout(adder_1_cout));  // open: cin
  Subtractor #(.width(32)) subtractor_1 (
    .a(in_2), .b(in_3), .out(subtractor_1_out), .bout(subtractor_1_bout));  // open: bin
  Multiplexer #(.width(32), .enable("false")) multiplexer_1 (
    .in0(adder_1_out), .in1(subtractor_1_out), .out(out_4), .sel(Add_Sub_control));
  Multiplexer #(.enable("false")) multiplexer_2 (
    .in0(adder_1_cout), .in1(subtractor_1_bout), .out(carry_out), .sel(Add_Sub_control));
endmodule

module ALU (
  input  [3:0] ALUCtl,
  input  [31:0] A,
  input  [31:0] B,
  input  [4:0] Shamt,
  output [31:0] ALUResult,
  output Zero,
  output Overflow
);

  wire comparator_1_lt, comparator_2_lt, comparator_3_eq, comparator_4_eq, or_2_out;
  wire [31:0] Add, And, LessThan, LessThanUnsigned, Nor, Or, ShiftLeft, ShiftRight, Sub, Xor;

  // Probe on ALUCtl
  assign Nor = ~(A | B);  // NOR_Gate nor_1, 32 bits wide
  Adder #(.width(32)) adder_1 (.a(A), .b(B), .out(Add));  // open: cin, cout
  Subtractor #(.width(32)) subtractor_1 (.a(A), .b(B), .out(Sub));  // open: bin, bout
  assign And = A & B;  // AND_Gate and_1, 32 bits wide
  assign Or = A | B;  // OR_Gate or_1, 32 bits wide
  assign Xor = A ^ B;  // XOR_Gate xor_1, 32 bits wide
  Comparator #(.width(32)) comparator_1 (.a(A), .b(B), .lt(comparator_1_lt));  // open: gt, eq
  assign LessThan = {{31{1'b0}}, comparator_1_lt};  // Bit_Extender bit_extender_1
  Shifter #(.width(32)) shifter_1 (.in(B), .\dist (Shamt), .out(ShiftLeft));
  Shifter #(.width(32), .shift("lr")) shifter_2 (.in(B), .\dist (Shamt), .out(ShiftRight));
  Comparator #(.width(32), .mode("unsigned")) comparator_2 (.a(A), .b(B), .lt(comparator_2_lt));  // open: gt, eq
  assign LessThanUnsigned = {{31{1'b0}}, comparator_2_lt};  // Bit_Extender bit_extender_2
  Multiplexer #(.select(4), .width(32), .enable("false")) multiplexer_1 (
    .in0(Or), .in1(LessThanUnsigned), .in2(LessThan), .in3(Add), .in4(Sub), .in5(Xor), .in6(And),
    .in14(ShiftRight), .in15(ShiftLeft), .out(ALUResult), .sel(ALUCtl));  // open: in7, in8, in9, in10, in11, in12, in13
  Comparator #(.width(4)) comparator_3 (.a(4'b0011), .b(ALUCtl), .eq(comparator_3_eq));  // open: gt, lt
  Comparator #(.width(4)) comparator_4 (.a(ALUCtl), .b(4'b0100), .eq(comparator_4_eq));  // open: gt, lt
  Overflow_Unit overflow_unit_1 (
    .Add(comparator_3_eq), .Sub(comparator_4_eq), .ASign(A[31]), .BSign(B[31]), .ResultSign(ALUResult[31]),
    .Overflow(Overflow));
  or or_2 (or_2_out, ALUResult[0], ALUResult[1], ALUResult[2], ALUResult[3], ALUResult[4], ALUResult[5], ALUResult[6], ALUResult[7], ALUResult[8], ALUResult[9], ALUResult[10], ALUResult[11], ALUResult[12], ALUResult[13], ALUResult[14], ALUResult[15], ALUResult[16], ALUResult[17], ALUResult[18], ALUResult[19], ALUResult[20], ALUResult[21], ALUResult[22], ALUResult[23], ALUResult[24], ALUResult[25], ALUResult[26], ALUResult[27], ALUResult[28], ALUResult[29], ALUResult[30], ALUResult[31]);
  not not_1 (Zero, or_2_out);

  // Other names for the same wires on the sheet: ASign = A[31]; ResultSign = ALUResult[31]; BSign = B[31]

  // Notes on the sheet:
  //   ALUCtl for ADD for top port
  //   ALUCtl for SUB for second port
endmodule

module Register_File (
  input  [4:0] WrAddr,
  input  [31:0] WrData,
  input  WrReg,
  input  [4:0] RdAddr1,
  input  [4:0] RdAddr2,
  input  Clock,
  output [31:0] RdData1,
  output [31:0] RdData2
);

  wire WrReg0, WrReg1, WrReg2, WrReg3, WrReg4, WrReg5, WrReg6, WrReg7, WrReg8, WrReg9, WrReg10, WrReg11,
       WrReg12, WrReg13, WrReg14, WrReg15, WrReg16, WrReg17, WrReg18, WrReg19, WrReg20, WrReg21, WrReg22,
       WrReg23, WrReg24, WrReg25, WrReg26, WrReg27, WrReg28, WrReg29, WrReg30, WrReg31;
  wire [31:0] RegData1, RegData2, RegData3, RegData4, RegData5, RegData6, RegData7, RegData8, RegData9,
       RegData10, RegData11, RegData12, RegData13, RegData14, RegData15, RegData16, RegData17, RegData18,
       RegData19, RegData20, RegData21, RegData22, RegData23, RegData24, RegData25, RegData26, RegData27,
       RegData28, RegData29, RegData30, RegData31;

  Demultiplexer #(.select(5), .enable("false")) demultiplexer_1 (
    .out0(WrReg0), .out1(WrReg1), .out2(WrReg2), .out3(WrReg3), .out4(WrReg4), .out5(WrReg5), .out6(WrReg6),
    .out7(WrReg7), .out8(WrReg8), .out9(WrReg9), .out10(WrReg10), .out11(WrReg11), .out12(WrReg12),
    .out13(WrReg13), .out14(WrReg14), .out15(WrReg15), .out16(WrReg16), .out17(WrReg17), .out18(WrReg18),
    .out19(WrReg19), .out20(WrReg20), .out21(WrReg21), .out22(WrReg22), .out23(WrReg23), .out24(WrReg24),
    .out25(WrReg25), .out26(WrReg26), .out27(WrReg27), .out28(WrReg28), .out29(WrReg29), .out30(WrReg30),
    .out31(WrReg31), .in(WrReg), .sel(WrAddr));
  // Probe on RegData4
  Register #(.width(32)) Reg4 (.D(WrData), .en(WrReg4), .Q(RegData4), .clk(Clock));  // open: clr
  // Probe on RegData8
  Register #(.width(32)) Reg8 (.D(WrData), .en(WrReg8), .Q(RegData8), .clk(Clock));  // open: clr
  // Probe on RegData12
  Register #(.width(32)) Reg12 (.D(WrData), .en(WrReg12), .Q(RegData12), .clk(Clock));  // open: clr
  // Probe on RegData16
  Register #(.width(32)) Reg16 (.D(WrData), .en(WrReg16), .Q(RegData16), .clk(Clock));  // open: clr
  // Probe on RegData20
  Register #(.width(32)) Reg20 (.D(WrData), .en(WrReg20), .Q(RegData20), .clk(Clock));  // open: clr
  // Probe on RegData24
  Register #(.width(32)) Reg24 (.D(WrData), .en(WrReg24), .Q(RegData24), .clk(Clock));  // open: clr
  // Probe on RegData28
  Register #(.width(32)) Reg28 (.D(WrData), .en(WrReg28), .Q(RegData28), .clk(Clock));  // open: clr
  Register #(.width(32)) Reg1 (.D(WrData), .en(WrReg1), .Q(RegData1), .clk(Clock));  // open: clr
  Register #(.width(32)) Reg5 (.D(WrData), .en(WrReg5), .Q(RegData5), .clk(Clock));  // open: clr
  Register #(.width(32)) Reg9 (.D(WrData), .en(WrReg9), .Q(RegData9), .clk(Clock));  // open: clr
  Register #(.width(32)) Reg13 (.D(WrData), .en(WrReg13), .Q(RegData13), .clk(Clock));  // open: clr
  Register #(.width(32)) Reg17 (.D(WrData), .en(WrReg17), .Q(RegData17), .clk(Clock));  // open: clr
  Register #(.width(32)) Reg21 (.D(WrData), .en(WrReg21), .Q(RegData21), .clk(Clock));  // open: clr
  Register #(.width(32)) Reg25 (.D(WrData), .en(WrReg25), .Q(RegData25), .clk(Clock));  // open: clr
  Register #(.width(32)) Reg29 (.D(WrData), .en(WrReg29), .Q(RegData29), .clk(Clock));  // open: clr
  // Probe on RegData1
  // Probe on RegData5
  // Probe on RegData9
  // Probe on RegData13
  // Probe on RegData17
  // Probe on RegData21
  // Probe on RegData25
  // Probe on RegData29
  // Probe on RegData2
  Register #(.width(32)) Reg2 (.D(WrData), .en(WrReg2), .Q(RegData2), .clk(Clock));  // open: clr
  // Probe on RegData6
  Register #(.width(32)) Reg6 (.D(WrData), .en(WrReg6), .Q(RegData6), .clk(Clock));  // open: clr
  // Probe on RegData10
  Register #(.width(32)) Reg10 (.D(WrData), .en(WrReg10), .Q(RegData10), .clk(Clock));  // open: clr
  // Probe on RegData14
  Register #(.width(32)) Reg14 (.D(WrData), .en(WrReg14), .Q(RegData14), .clk(Clock));  // open: clr
  // Probe on RegData18
  Register #(.width(32)) Reg18 (.D(WrData), .en(WrReg18), .Q(RegData18), .clk(Clock));  // open: clr
  // Probe on RegData22
  Register #(.width(32)) Reg22 (.D(WrData), .en(WrReg22), .Q(RegData22), .clk(Clock));  // open: clr
  // Probe on RegData26
  Register #(.width(32)) Reg26 (.D(WrData), .en(WrReg26), .Q(RegData26), .clk(Clock));  // open: clr
  // Probe on RegData30
  Register #(.width(32)) Reg30 (.D(WrData), .en(WrReg30), .Q(RegData30), .clk(Clock));  // open: clr
  // Probe on RegData3
  Register #(.width(32)) Reg3 (.D(WrData), .en(WrReg3), .Q(RegData3), .clk(Clock));  // open: clr
  // Probe on RegData7
  Register #(.width(32)) Reg7 (.D(WrData), .en(WrReg7), .Q(RegData7), .clk(Clock));  // open: clr
  // Probe on RegData11
  Register #(.width(32)) Reg11 (.D(WrData), .en(WrReg11), .Q(RegData11), .clk(Clock));  // open: clr
  // Probe on RegData15
  Register #(.width(32)) Reg15 (.D(WrData), .en(WrReg15), .Q(RegData15), .clk(Clock));  // open: clr
  // Probe on RegData19
  Register #(.width(32)) Reg19 (.D(WrData), .en(WrReg19), .Q(RegData19), .clk(Clock));  // open: clr
  // Probe on RegData23
  Register #(.width(32)) Reg23 (.D(WrData), .en(WrReg23), .Q(RegData23), .clk(Clock));  // open: clr
  // Probe on RegData27
  Register #(.width(32)) Reg27 (.D(WrData), .en(WrReg27), .Q(RegData27), .clk(Clock));  // open: clr
  // Probe on RegData31
  Register #(.width(32)) Reg31 (.D(WrData), .en(WrReg31), .Q(RegData31), .clk(Clock));  // open: clr
  Multiplexer #(.select(5), .width(32), .enable("false")) multiplexer_1 (
    .in0({32{1'b0}}), .in1(RegData1), .in2(RegData2), .in3(RegData3), .in4(RegData4), .in5(RegData5),
    .in6(RegData6), .in7(RegData7), .in8(RegData8), .in9(RegData9), .in10(RegData10), .in11(RegData11),
    .in12(RegData12), .in13(RegData13), .in14(RegData14), .in15(RegData15), .in16(RegData16),
    .in17(RegData17), .in18(RegData18), .in19(RegData19), .in20(RegData20), .in21(RegData21),
    .in22(RegData22), .in23(RegData23), .in24(RegData24), .in25(RegData25), .in26(RegData26),
    .in27(RegData27), .in28(RegData28), .in29(RegData29), .in30(RegData30), .in31(RegData31), .out(RdData1),
    .sel(RdAddr1));
  Multiplexer #(.select(5), .width(32), .enable("false")) multiplexer_2 (
    .in0({32{1'b0}}), .in1(RegData1), .in2(RegData2), .in3(RegData3), .in4(RegData4), .in5(RegData5),
    .in6(RegData6), .in7(RegData7), .in8(RegData8), .in9(RegData9), .in10(RegData10), .in11(RegData11),
    .in12(RegData12), .in13(RegData13), .in14(RegData14), .in15(RegData15), .in16(RegData16),
    .in17(RegData17), .in18(RegData18), .in19(RegData19), .in20(RegData20), .in21(RegData21),
    .in22(RegData22), .in23(RegData23), .in24(RegData24), .in25(RegData25), .in26(RegData26),
    .in27(RegData27), .in28(RegData28), .in29(RegData29), .in30(RegData30), .in31(RegData31), .out(RdData2),
    .sel(RdAddr2));
endmodule

module Overflow_Unit (
  input  Add,
  input  Sub,
  input  ASign,
  input  BSign,
  input  ResultSign,
  output Overflow
);

  wire and_1_out, and_2_out, or_1_out, xnor_1_out, xor_1_out, xor_2_out;

  xnor xnor_1 (xnor_1_out, ASign, BSign);
  xor xor_1 (xor_1_out, ASign, BSign);
  and and_1 (and_1_out, xnor_1_out, Add);
  and and_2 (and_2_out, xor_1_out, Sub);
  or or_1 (or_1_out, and_1_out, and_2_out);
  xor xor_2 (xor_2_out, ResultSign, ASign);
  and and_3 (Overflow, or_1_out, xor_2_out);

  // Notes on the sheet:
  //   Overflow occurs when doing addition and sign(A) == sign(B) && sign(result) != sign(A)
  //   Or
  //   Overflow occurs when doing subtraction and sign(A) != sign(B) && sign(result) != sign(A)
endmodule

module ALUCtrR (
  input  f5,
  input  f4,
  input  f3,
  input  f2,
  input  f1,
  input  f0,
  output c3,
  output c2,
  output c1,
  output c0
);

  wire and_1_out, and_2_out, and_3_out, and_4_out, and_5_out, and_6_out, and_7_out, and_8_out, and_9_out,
       and_10_out, and_11_out, and_12_out, and_13_out, and_14_out, and_15_out, and_16_out, and_17_out,
       and_18_out, and_19_out, and_20_out, and_21_out, and_22_out, not_1_out, not_2_out, not_3_out,
       not_4_out, not_5_out, not_6_out, not_7_out, not_8_out, not_9_out, not_10_out, not_11_out, not_12_out,
       not_13_out, not_14_out, not_15_out, not_16_out, not_17_out, not_18_out, not_19_out, not_20_out,
       not_21_out, not_22_out, not_23_out, not_24_out, not_25_out, not_26_out, not_27_out, not_28_out;

  not not_1 (not_1_out, f5);
  not not_2 (not_2_out, f3);
  not not_3 (not_3_out, f5);
  not not_4 (not_4_out, f5);
  not not_5 (not_5_out, f5);
  not not_6 (not_6_out, f5);
  not not_7 (not_7_out, f5);
  not not_8 (not_8_out, f3);
  not not_9 (not_9_out, f5);
  not not_10 (not_10_out, f5);
  not not_11 (not_11_out, f3);
  not not_12 (not_12_out, f0);
  not not_13 (not_13_out, f5);
  not not_14 (not_14_out, f5);
  not not_15 (not_15_out, f3);
  not not_16 (not_16_out, f5);
  not not_17 (not_17_out, f5);
  not not_18 (not_18_out, f0);
  not not_19 (not_19_out, f0);
  not not_20 (not_20_out, f1);
  not not_21 (not_21_out, f0);
  not not_22 (not_22_out, f3);
  not not_23 (not_23_out, f2);
  not not_24 (not_24_out, f1);
  not not_25 (not_25_out, f2);
  not not_26 (not_26_out, f1);
  not not_27 (not_27_out, f2);
  not not_28 (not_28_out, f1);
  and and_1 (and_1_out, not_1_out, not_2_out);
  and and_2 (and_2_out, not_3_out, f0);
  and and_3 (and_3_out, not_4_out, f1);
  and and_4 (and_4_out, not_5_out, f2);
  and and_5 (and_5_out, not_6_out, f4);
  and and_6 (and_6_out, not_7_out, not_8_out);
  and and_7 (and_7_out, not_9_out, f0);
  and and_8 (and_8_out, not_10_out, f1);
  and and_9 (and_9_out, not_11_out, f1);
  and and_10 (and_10_out, f2, not_12_out);
  and and_11 (and_11_out, not_13_out, f4);
  and and_12 (and_12_out, not_14_out, not_15_out);
  and and_13 (and_13_out, not_16_out, f0);
  and and_14 (and_14_out, not_17_out, f2);
  and and_15 (and_15_out, f3, f1, not_18_out);
  and and_16 (and_16_out, f4, f3, not_19_out);
  and and_17 (and_17_out, f5, not_20_out, not_21_out);
  and and_18 (and_18_out, not_22_out, not_23_out, not_24_out);
  and and_19 (and_19_out, f2, f1);
  and and_20 (and_20_out, f3, f0);
  and and_21 (and_21_out, f4, not_25_out, not_26_out);
  and and_22 (and_22_out, f5, not_27_out, not_28_out);
  or or_1 (c3, and_1_out, and_2_out, and_3_out, and_4_out, and_5_out);
  or or_2 (c2, and_6_out, and_7_out, and_8_out, and_9_out, and_10_out, and_11_out);
  or or_3 (c1, and_12_out, and_13_out, and_14_out, and_15_out, and_16_out, and_17_out);
  or or_4 (c0, and_18_out, and_19_out, and_20_out, and_21_out, and_22_out);
endmodule

module PC (
  input  [31:0] PCInput,
  input  PC_PAUSE,
  input  CLOCK,
  input  PC_RESET,
  input  Add_Sub_Ctrl,
  input  BEQ,
  input  [31:0] BEQOprand,
  output [31:0] NEXT_PC_Addr,
  output [31:0] PC_Addr,
  output Carry_Out
);

  wire [31:0] multiplexer_1_out, n32_bit_adder_subtractor_1_out_4;

  _32_Bit_Adder_Subtractor u_32_bit_adder_subtractor_1 (
    .Add_Sub_control(1'b0), .in_2(32'h4), .in_3(BEQOprand), .out_4(n32_bit_adder_subtractor_1_out_4));  // open: carry_out
  Register #(.width(32)) register_1 (.D(PCInput), .en(PC_PAUSE), .Q(PC_Addr), .clk(CLOCK), .clr(PC_RESET));
  _32_Bit_Adder_Subtractor u_32_bit_adder_subtractor_2 (
    .Add_Sub_control(Add_Sub_Ctrl), .in_2(PC_Addr), .in_3(multiplexer_1_out), .out_4(NEXT_PC_Addr),
    .carry_out(Carry_Out));
  Multiplexer #(.width(32), .enable("false")) multiplexer_1 (
    .in0(32'h4), .in1(n32_bit_adder_subtractor_1_out_4), .out(multiplexer_1_out), .sel(BEQ));
endmodule

module MUXsel (
  input  op5,
  input  op4,
  input  op3,
  input  op2,
  input  op1,
  input  op0,
  output MuxS
);

  wire not_1_out, not_2_out, not_3_out, not_4_out, not_5_out, not_6_out;

  not not_1 (not_1_out, op5);
  not not_2 (not_2_out, op4);
  not not_3 (not_3_out, op3);
  not not_4 (not_4_out, op2);
  not not_5 (not_5_out, op1);
  not not_6 (not_6_out, op0);
  and and_1 (MuxS, not_1_out, not_2_out, not_3_out, not_4_out, not_5_out, not_6_out);
endmodule

module _16to32SignExtention (
  input  [15:0] in_1,
  output [31:0] out_2
);

  and and_1 (out_2[31], in_1[15], 1'b1);

  assign out_2[30:0] = {{15{out_2[31]}}, in_1};
endmodule

module CombWrReg (
  input  op5,
  input  op4,
  input  op3,
  input  op2,
  input  op1,
  input  op0,
  output RegW
);

  wire and_1_out, and_2_out, and_3_out, not_1_out, not_2_out, not_3_out, not_4_out, not_5_out, not_6_out,
       not_7_out, not_8_out, not_9_out, not_10_out, not_11_out;

  not not_1 (not_1_out, op5);
  not not_2 (not_2_out, op4);
  not not_3 (not_3_out, op2);
  not not_4 (not_4_out, op1);
  not not_5 (not_5_out, op0);
  not not_6 (not_6_out, op4);
  not not_7 (not_7_out, op3);
  not not_8 (not_8_out, op2);
  not not_9 (not_9_out, op5);
  not not_10 (not_10_out, op4);
  not not_11 (not_11_out, op1);
  and and_1 (and_1_out, not_1_out, not_2_out, not_3_out, not_4_out, not_5_out);
  and and_2 (and_2_out, not_6_out, not_7_out, not_8_out, op1, op0);
  and and_3 (and_3_out, not_9_out, not_10_out, op3, op2, not_11_out);
  or or_1 (RegW, and_1_out, and_2_out, and_3_out);
endmodule

module isEqual (
  input  [31:0] in_1,
  output out_2
);

  wire [31:0] not_1_out;

  assign not_1_out = ~in_1;  // NOT_Gate not_1, 32 bits wide
  and and_1 (out_2, not_1_out[0], not_1_out[1], not_1_out[2], not_1_out[3], not_1_out[4], not_1_out[5], not_1_out[6], not_1_out[7], not_1_out[8], not_1_out[9], not_1_out[10], not_1_out[11], not_1_out[12], not_1_out[13], not_1_out[14], not_1_out[15], not_1_out[16], not_1_out[17], not_1_out[18], not_1_out[19], not_1_out[20], not_1_out[21], not_1_out[22], not_1_out[23], not_1_out[24], not_1_out[25], not_1_out[26], not_1_out[27], not_1_out[28], not_1_out[29], not_1_out[30], not_1_out[31]);
endmodule

module IJALUCtr (
  input  op5,
  input  op4,
  input  op3,
  input  op2,
  input  op1,
  input  op0,
  output c3,
  output c2,
  output c1,
  output c0
);

  wire and_2_out, not_1_out, not_2_out, not_3_out, not_4_out;

  not not_1 (not_1_out, op0);
  not not_2 (not_2_out, op0);
  not not_3 (not_3_out, op3);
  not not_4 (not_4_out, op2);
  and and_1 (c2, op2, not_1_out);
  and and_2 (and_2_out, op3, not_2_out);
  or or_1 (c0, not_3_out, not_4_out);
  or or_2 (c1, op1, and_2_out);

  assign c3 = 1'b0;
endmodule

module CombStr (
  input  op5,
  input  op4,
  input  op3,
  input  op2,
  input  op1,
  input  op0,
  output str
);

  wire not_1_out, not_2_out;

  not not_1 (not_1_out, op4);
  not not_2 (not_2_out, op2);
  and and_1 (str, op5, not_1_out, op3, not_2_out, op1, op0);
endmodule

module CombWrData (
  input  op5,
  input  op4,
  input  op3,
  input  op2,
  input  op1,
  input  op0,
  output W1,
  output W2
);

  wire not_1_out, not_2_out, not_3_out, not_4_out, not_5_out, not_6_out, not_7_out;

  not not_1 (not_1_out, op5);
  not not_2 (not_2_out, op4);
  not not_3 (not_3_out, op3);
  not not_4 (not_4_out, op2);
  not not_5 (not_5_out, op4);
  not not_6 (not_6_out, op3);
  not not_7 (not_7_out, op2);
  and and_1 (W1, not_1_out, not_2_out, not_3_out, not_4_out, op1, op0);
  and and_2 (W2, not_5_out, not_6_out, not_7_out, op1, op0);
endmodule

module CombJAL (
  input  op5,
  input  op4,
  input  op3,
  input  op2,
  input  op1,
  input  op0,
  output JAL
);

  wire not_1_out, not_2_out, not_3_out, not_4_out;

  not not_1 (not_1_out, op5);
  not not_2 (not_2_out, op4);
  not not_3 (not_3_out, op3);
  not not_4 (not_4_out, op2);
  and and_1 (JAL, not_1_out, not_2_out, not_3_out, not_4_out, op1, op0);
endmodule

module _26to32labelExtention (
  input  [25:0] in_1,
  output [31:0] out_2
);


  assign out_2 = {{6{1'b0}}, in_1};
endmodule

module isJR (
  input  func5,
  input  func4,
  input  func3,
  input  func2,
  input  func1,
  input  func0,
  output true
);

  wire not_1_out, not_2_out, not_3_out, not_4_out, not_5_out;

  not not_1 (not_1_out, func5);
  not not_2 (not_2_out, func4);
  not not_3 (not_3_out, func2);
  not not_4 (not_4_out, func1);
  not not_5 (not_5_out, func0);
  and and_1 (true, not_1_out, not_2_out, func3, not_3_out, not_4_out, not_5_out);
endmodule

module isJ_JAL (
  input  op5,
  input  op4,
  input  op3,
  input  op2,
  input  op1,
  input  op0,
  output true
);

  wire not_1_out, not_2_out, not_3_out, not_4_out;

  not not_1 (not_1_out, op5);
  not not_2 (not_2_out, op4);
  not not_3 (not_3_out, op3);
  not not_4 (not_4_out, op2);
  and and_1 (true, not_1_out, not_2_out, not_3_out, not_4_out, op1);
endmodule

module isBEQ (
  input  op5,
  input  op4,
  input  op3,
  input  op2,
  input  op1,
  input  op0,
  output true
);

  wire not_1_out, not_2_out, not_3_out, not_4_out, not_5_out;

  not not_1 (not_1_out, op5);
  not not_2 (not_2_out, op4);
  not not_3 (not_3_out, op3);
  not not_4 (not_4_out, op1);
  not not_5 (not_5_out, op0);
  and and_1 (true, not_1_out, not_2_out, not_3_out, op2, not_4_out, not_5_out);
endmodule

module pCMuxCtr (
  input  isBEQ,
  input  isJR,
  input  isJJAL,
  input  isEqual,
  output ctr1,
  output ctr0
);

  wire and_1_out;

  or or_1 (ctr1, isJJAL, isJR);
  and and_1 (and_1_out, isBEQ, isEqual);
  or or_2 (ctr0, isJR, and_1_out);
endmodule

module _32shif2 (
  input  [31:0] in_1,
  output [31:0] out_2
);


  assign out_2 = {in_1[29:0], 2'b00};
endmodule
