// Logisim project Lab3_with_logic_separation.circ as structural Verilog: 13 circuits, main circuit Main
module Main (
);

  wire Branch, CLK, control_1_alusrca, control_1_iord, control_1_irwrite, MemRead, MemWrite, PCEnable,
       RegWrite, ZERO;
  wire [1:0] ALUOp, ALUSrcB, control_1_memtoreg0, control_1_regdst0, PCSource;
  wire [2:0] NSS;
  wire [2:1] control_1_pcwritecond;
  wire [3:0] adder_1_out, alucontrol_1_aluctrl, dispatchrom1_1_nextstate, dispatchrom2_1_nextstate,
       dispatchrom3_1_nextstate, multiplexer_4_out, state;
  wire [4:0] WrAddr;
  wire [5:0] func;
  wire [6:0] bitselector_2_out, PCR1;
  wire [7:0] multiplexer_1_out, PCR2;
  wire [15:6] Imm;
  wire [25:0] bitselector_3_out;
  wire [31:0] A, alu_1_aluresult, ALUOut_q, B, MDR_q, MemData, multiplexer_7_out, n16to32se_1_out_2,
       n26to32_1_out_2, PC, RA, ram_1_data, register_file_1_rddata1, register_file_1_rddata2, shifter_2_out,
       shifter_3_out, wd;
  wire [31:16] IR;

  Clock clock_1 (.out(CLK));
  Register #(.width(32)) u_PC (.D(multiplexer_7_out), .en(PCEnable), .Q(PC), .clk(CLK));  // open: clr
  BitSelector #(.width(32), .group(7)) bitselector_1 (.in(PC), .out(PCR1), .sel(3'b000));
  Multiplexer #(.width(8), .enable("false")) multiplexer_1 (
    .in0(PCR2), .in1({1'b1, bitselector_2_out}), .out(multiplexer_1_out), .sel(control_1_iord));
  DispatchROM4 dispatchrom4_1 (.in({control_1_pcwritecond, ZERO}), .PCEnable(PCEnable));
  Shifter #(.shift("lr")) shifter_1 (.in({1'b0, PCR1}), .\dist (3'b010), .out(PCR2));
  RAM #(.dataWidth(32), .bus("separate")) ram_1 (
    .addr(multiplexer_1_out), .din(MemData), .data(ram_1_data), .str(MemWrite), .clk(CLK), .ld(MemRead));  // open: sel, clr
  BitSelector #(.width(32), .group(7)) bitselector_2 (.in(ALUOut_q), .out(bitselector_2_out), .sel(3'b000));
  Register #(.width(32)) u_IR (.D(ram_1_data), .en(control_1_irwrite), .Q({IR, Imm, func}), .clk(CLK));  // open: clr
  Register #(.width(32)) MDR (.D(ram_1_data), .Q(MDR_q), .clk(CLK));  // open: en, clr
  and and_1 (Branch, ZERO, control_1_pcwritecond[1]);
  Multiplexer #(.select(2), .width(5), .enable("false")) multiplexer_2 (
    .in0(IR[20:16]), .in1(Imm[15:11]), .in2({5{1'b1}}), .out(WrAddr), .sel(control_1_regdst0));  // open: in3
  Multiplexer #(.select(2), .width(32), .enable("false")) multiplexer_3 (
    .in0(ALUOut_q), .in1(MDR_q), .in2(PC), .out(wd), .sel(control_1_memtoreg0));  // open: in3
  Control control_1 (
    .NextStateSrc(NSS), .Current_State(state), .MemtoReg0(control_1_memtoreg0[0]),
    .RegDst0(control_1_regdst0[0]), .RegWrite(RegWrite), .ALUSrcA(control_1_alusrca), .ALUSrcB0(ALUSrcB[0]),
    .ALUSrcB1(ALUSrcB[1]), .ALUOp0(ALUOp[0]), .ALUOp1(ALUOp[1]), .PCSource0(PCSource[0]),
    .PCSource1(PCSource[1]), .IRWrite(control_1_irwrite), .MemtoReg1(control_1_memtoreg0[1]),
    .MemWrite(MemWrite), .MemRead(MemRead), .IorD(control_1_iord), .PCWrite(control_1_pcwritecond[2]),
    .PCWriteCond(control_1_pcwritecond[1]), .RegDst1(control_1_regdst0[1]));
  Register_File register_file_1 (
    .WrAddr(WrAddr), .WrData(wd), .WrReg(RegWrite), .RdAddr1(IR[25:21]), .RdAddr2(IR[20:16]),
    .RdData1(register_file_1_rddata1), .RdData2(register_file_1_rddata2), .Clock(CLK));
  Adder #(.width(4)) adder_1 (.a(state), .b(4'b0001), .out(adder_1_out));  // open: cin, cout
  DispatchROM1 dispatchrom1_1 (.op(IR[31:26]), .NextState(dispatchrom1_1_nextstate));
  DispatchROM2 dispatchrom2_1 (.op(IR[31:26]), .NextState(dispatchrom2_1_nextstate));
  DispatchROM3 dispatchrom3_1 (.func(func), .NextState(dispatchrom3_1_nextstate));
  Register #(.width(32)) u_A (.D(register_file_1_rddata1), .Q(RA), .clk(CLK));  // open: en, clr
  Register #(.width(32)) u_B (.D(register_file_1_rddata2), .Q(MemData), .clk(CLK));  // open: en, clr
  _16to32SE u_16to32se_1 (.in_1({Imm, func}), .out_2(n16to32se_1_out_2));
  Multiplexer #(.select(3), .width(4), .enable("false")) multiplexer_4 (
    .in0(adder_1_out), .in1(dispatchrom1_1_nextstate), .in2(dispatchrom2_1_nextstate),
    .in3(dispatchrom3_1_nextstate), .in7(4'b0000), .out(multiplexer_4_out), .sel(NSS));  // open: in4, in5, in6
  Multiplexer #(.width(32), .enable("false")) multiplexer_5 (.in0(PC), .in1(RA), .out(A), .sel(control_1_alusrca));
  Register #(.width(4)) IR_2 (.D(multiplexer_4_out), .Q(state), .clk(CLK));  // open: en, clr
  _26to32 u_26to32_1 (.in_1(bitselector_3_out), .out_2(n26to32_1_out_2));
  BitSelector #(.width(32), .group(26)) bitselector_3 (.in({IR, Imm, func}), .out(bitselector_3_out), .sel(1'b0));
  Multiplexer #(.select(2), .width(32), .enable("false")) multiplexer_6 (
    .in0(MemData), .in1(32'h4), .in2(n16to32se_1_out_2), .in3(shifter_2_out), .out(B), .sel(ALUSrcB));
  Shifter #(.width(32)) shifter_2 (.in(n16to32se_1_out_2), .\dist (5'b00010), .out(shifter_2_out));
  // Probe on A
  ALUControl alucontrol_1 (.ALUOp(ALUOp), .func(func), .op(IR[31:26]), .ALUCtrl(alucontrol_1_aluctrl));
  ALU alu_1 (
    .ALUCtl(alucontrol_1_aluctrl), .A(A), .B(B), .ALUResult(alu_1_aluresult), .Zero(ZERO), .Shamt(Imm[10:6]));  // open: Overflow
  // Probe on Imm[10:6]
  // Probe on B
  Shifter #(.width(32)) shifter_3 (.in(n26to32_1_out_2), .\dist (5'b00010), .out(shifter_3_out));
  // Probe on alu_1_aluresult
  // Probe on PC
  // Probe on RegWrite
  // Probe on WrAddr
  // Probe on wd
  // Probe on MemWrite
  // Probe on MemData
  // Probe on Branch
  Register #(.width(32)) ALUOut (.D(alu_1_aluresult), .Q(ALUOut_q), .clk(CLK));  // open: en, clr
  Multiplexer #(.select(2), .width(32), .enable("false")) multiplexer_7 (
    .in0(alu_1_aluresult), .in1(ALUOut_q), .in2(shifter_3_out), .in3(RA), .out(multiplexer_7_out),
    .sel(PCSource));

  // Other names for the same wires on the sheet: Imm[5:0] = func; IR[15:0] = {Imm, func}; Shamt[4:0] = Imm[10:6];
  //   Rd[4:0] = Imm[15:11]; Rt[4:0] = IR[20:16]; Rs[4:0] = IR[25:21]; op[5:0] = IR[31:26]

  // Notes on the sheet:
  //   J type
  //   I type
  //   R type
endmodule

module _32_Bit_Adder___Subtractor (
  input  Add_Sub_control,
  input  [31:0] in_2,
  input  [31:0] in_3,
  output [31:0] out_4,
  output carry_out
);

  wire adder_1_cout, subtractor_1_bout;
  wire [31:0] adder_1_out, subtractor_1_out;

  Adder #(.width(32)) adder_1 (.a(in_2), .b(in_3), .out(adder_1_out), .cout(adder_1_cout));  // open: cin
  Subtractor #(.width(32)) subtractor_1 (
    .a(in_2), .b(in_3), .out(subtractor_1_out), .bout(subtractor_1_bout));  // open: bin
  Multiplexer #(.width(32), .enable("false")) multiplexer_1 (
    .in0(adder_1_out), .in1(subtractor_1_out), .out(out_4), .sel(Add_Sub_control));
  Multiplexer #(.enable("false")) multiplexer_2 (
    .in0(adder_1_cout), .in1(subtractor_1_bout), .out(carry_out), .sel(Add_Sub_control));
endmodule

module ALU (
  input  [3:0] ALUCtl,
  input  [31:0] A,
  input  [31:0] B,
  input  [4:0] Shamt,
  output [31:0] ALUResult,
  output Zero,
  output Overflow
);

  wire comparator_1_lt, comparator_2_lt, comparator_3_eq, comparator_4_eq, or_2_out;
  wire [31:0] Add, And, LessThan, LessThanUnsigned, Nor, Or, ShiftLeft, ShiftRight, Sub, Xor;

  // Probe on ALUCtl
  assign Nor = ~(A | B);  // NOR_Gate nor_1, 32 bits wide
  Adder #(.width(32)) adder_1 (.a(A), .b(B), .out(Add));  // open: cin, cout
  Subtractor #(.width(32)) subtractor_1 (.a(A), .b(B), .out(Sub));  // open: bin, bout
  assign And = A & B;  // AND_Gate and_1, 32 bits wide
  assign Or = A | B;  // OR_Gate or_1, 32 bits wide
  assign Xor = A ^ B;  // XOR_Gate xor_1, 32 bits wide
  Comparator #(.width(32)) comparator_1 (.a(A), .b(B), .lt(comparator_1_lt));  // open: gt, eq
  assign LessThan = {{31{1'b0}}, comparator_1_lt};  // Bit_Extender bit_extender_1
  Shifter #(.width(32)) shifter_1 (.in(B), .\dist (Shamt), .out(ShiftLeft));
  Shifter #(.width(32), .shift("lr")) shifter_2 (.in(B), .\dist (Shamt), .out(ShiftRight));
  Comparator #(.width(32), .mode("unsigned")) comparator_2 (.a(A), .b(B), .lt(comparator_2_lt));  // open: gt, eq
  assign LessThanUnsigned = {{31{1'b0}}, comparator_2_lt};  // Bit_Extender bit_extender_2
  Multiplexer #(.select(4), .width(32), .enable("false")) multiplexer_1 (
    .in0(Or), .in1(LessThanUnsigned), .in2(LessThan), .in3(Add), .in4(Sub), .in5(Xor), .in6(And),
    .in14(ShiftRight), .in15(ShiftLeft), .out(ALUResult), .sel(ALUCtl));  // open: in7, in8, in9, in10, in11, in12, in13
  Comparator #(.width(4)) comparator_3 (.a(4'b0011), .b(ALUCtl), .eq(comparator_3_eq));  // open: gt, lt
  Comparator #(.width(4)) comparator_4 (.a(ALUCtl), .b(4'b0100), .eq(comparator_4_eq));  // open: gt, lt
  Overflow overflow_1 (
    .Add(comparator_3_eq), .Sub(comparator_4_eq), .ASign(A[31]), .BSign(B[31]), .ResultSign(ALUResult[31]),
    .Overflow(Overflow));
  or or_2 (or_2_out, ALUResult[0], ALUResult[1], ALUResult[2], ALUResult[3], ALUResult[4], ALUResult[5], ALUResult[6], ALUResult[7], ALUResult[8], ALUResult[9], ALUResult[10], ALUResult[11], ALUResult[12], ALUResult[13], ALUResult[14], ALUResult[15], ALUResult[16], ALUResult[17], ALUResult[18], ALUResult[19], ALUResult[20], ALUResult[21], ALUResult[22], ALUResult[23], ALUResult[24], ALUResult[25], ALUResult[26], ALUResult[27], ALUResult[28], ALUResult[29], ALUResult[30], ALUResult[31]);
  not not_1 (Zero, or_2_out);

  // Other names for the same wires on the sheet: ASign = A[31]; ResultSign = ALUResult[31]; BSign = B[31]
endmodule

module Register_File (
  input  [4:0] WrAddr,
  input  [31:0] WrData,
  input  WrReg,
  input  [4:0] RdAddr1,
  input  [4:0] RdAddr2,
  input  Clock,
  output [31:0] RdData1,
  output [31:0] RdData2
);

  wire WrReg0, WrReg1, WrReg2, WrReg3, WrReg4, WrReg5, WrReg6, WrReg7, WrReg8, WrReg9, WrReg10, WrReg11,
       WrReg12, WrReg13, WrReg14, WrReg15, WrReg16, WrReg17, WrReg18, WrReg19, WrReg20, WrReg21, WrReg22,
       WrReg23, WrReg24, WrReg25, WrReg26, WrReg27, WrReg28, WrReg29, WrReg30, WrReg31;
  wire [31:0] RegData1, RegData2, RegData3, RegData4, RegData5, RegData6, RegData7, RegData8, RegData9,
       RegData10, RegData11, RegData12, RegData13, RegData14, RegData15, RegData16, RegData17, RegData18,
       RegData19, RegData20, RegData21, RegData22, RegData23, RegData24, RegData25, RegData26, RegData27,
       RegData28, RegData29, RegData30, RegData31;

  Demultiplexer #(.select(5), .enable("false")) demultiplexer_1 (
    .out0(WrReg0), .out1(WrReg1), .out2(WrReg2), .out3(WrReg3), .out4(WrReg4), .out5(WrReg5), .out6(WrReg6),
    .out7(WrReg7), .out8(WrReg8), .out9(WrReg9), .out10(WrReg10), .out11(WrReg11), .out12(WrReg12),
    .out13(WrReg13), .out14(WrReg14), .out15(WrReg15), .out16(WrReg16), .out17(WrReg17), .out18(WrReg18),
    .out19(WrReg19), .out20(WrReg20), .out21(WrReg21), .out22(WrReg22), .out23(WrReg23), .out24(WrReg24),
    .out25(WrReg25), .out26(WrReg26), .out27(WrReg27), .out28(WrReg28), .out29(WrReg29), .out30(WrReg30),
    .out31(WrReg31), .in(WrReg), .sel(WrAddr));
  // Probe on RegData4
  Register #(.width(32)) Reg4 (.D(WrData), .en(WrReg4), .Q(RegData4), .clk(Clock));  // open: clr
  // Probe on RegData8
  Register #(.width(32)) Reg8 (.D(WrData), .en(WrReg8), .Q(RegData8), .clk(Clock));  // open: clr
  // Probe on RegData12
  Register #(.width(32)) Reg12 (.D(WrData), .en(WrReg12), .Q(RegData12), .clk(Clock));  // open: clr
  // Probe on RegData16
  Register #(.width(32)) Reg16 (.D(WrData), .en(WrReg16), .Q(RegData16), .clk(Clock));  // open: clr
  // Probe on RegData20
  Register #(.width(32)) Reg20 (.D(WrData), .en(WrReg20), .Q(RegData20), .clk(Clock));  // open: clr
  // Probe on RegData24
  Register #(.width(32)) Reg24 (.D(WrData), .en(WrReg24), .Q(RegData24), .clk(Clock));  // open: clr
  // Probe on RegData28
  Register #(.width(32)) Reg28 (.D(WrData), .en(WrReg28), .Q(RegData28), .clk(Clock));  // open: clr
  Register #(.width(32)) Reg1 (.D(WrData), .en(WrReg1), .Q(RegData1), .clk(Clock));  // open: clr
  Register #(.width(32)) Reg5 (.D(WrData), .en(WrReg5), .Q(RegData5), .clk(Clock));  // open: clr
  Register #(.width(32)) Reg9 (.D(WrData), .en(WrReg9), .Q(RegData9), .clk(Clock));  // open: clr
  Register #(.width(32)) Reg13 (.D(WrData), .en(WrReg13), .Q(RegData13), .clk(Clock));  // open: clr
  Register #(.width(32)) Reg17 (.D(WrData), .en(WrReg17), .Q(RegData17), .clk(Clock));  // open: clr
  Register #(.width(32)) Reg21 (.D(WrData), .en(WrReg21), .Q(RegData21), .clk(Clock));  // open: clr
  Register #(.width(32)) Reg25 (.D(WrData), .en(WrReg25), .Q(RegData25), .clk(Clock));  // open: clr
  Register #(.width(32)) Reg29 (.D(WrData), .en(WrReg29), .Q(RegData29), .clk(Clock));  // open: clr
  // Probe on RegData1
  // Probe on RegData5
  // Probe on RegData9
  // Probe on RegData13
  // Probe on RegData17
  // Probe on RegData21
  // Probe on RegData25
  // Probe on RegData29
  // Probe on RegData2
  Register #(.width(32)) Reg2 (.D(WrData), .en(WrReg2), .Q(RegData2), .clk(Clock));  // open: clr
  // Probe on RegData6
  Register #(.width(32)) Reg6 (.D(WrData), .en(WrReg6), .Q(RegData6), .clk(Clock));  // open: clr
  // Probe on RegData10
  Register #(.width(32)) Reg10 (.D(WrData), .en(WrReg10), .Q(RegData10), .clk(Clock));  // open: clr
  // Probe on RegData14
  Register #(.width(32)) Reg14 (.D(WrData), .en(WrReg14), .Q(RegData14), .clk(Clock));  // open: clr
  // Probe on RegData18
  Register #(.width(32)) Reg18 (.D(WrData), .en(WrReg18), .Q(RegData18), .clk(Clock));  // open: clr
  // Probe on RegData22
  Register #(.width(32)) Reg22 (.D(WrData), .en(WrReg22), .Q(RegData22), .clk(Clock));  // open: clr
  // Probe on RegData26
  Register #(.width(32)) Reg26 (.D(WrData), .en(WrReg26), .Q(RegData26), .clk(Clock));  // open: clr
  // Probe on RegData30
  Register #(.width(32)) Reg30 (.D(WrData), .en(WrReg30), .Q(RegData30), .clk(Clock));  // open: clr
  // Probe on RegData3
  Register #(.width(32)) Reg3 (.D(WrData), .en(WrReg3), .Q(RegData3), .clk(Clock));  // open: clr
  // Probe on RegData7
  Register #(.width(32)) Reg7 (.D(WrData), .en(WrReg7), .Q(RegData7), .clk(Clock));  // open: clr
  // Probe on RegData11
  Register #(.width(32)) Reg11 (.D(WrData), .en(WrReg11), .Q(RegData11), .clk(Clock));  // open: clr
  // Probe on RegData15
  Register #(.width(32)) Reg15 (.D(WrData), .en(WrReg15), .Q(RegData15), .clk(Clock));  // open: clr
  // Probe on RegData19
  Register #(.width(32)) Reg19 (.D(WrData), .en(WrReg19), .Q(RegData19), .clk(Clock));  // open: clr
  // Probe on RegData23
  Register #(.width(32)) Reg23 (.D(WrData), .en(WrReg23), .Q(RegData23), .clk(Clock));  // open: clr
  // Probe on RegData27
  Register #(.width(32)) Reg27 (.D(WrData), .en(WrReg27), .Q(RegData27), .clk(Clock));  // open: clr
  // Probe on RegData31
  Register #(.width(32)) Reg31 (.D(WrData), .en(WrReg31), .Q(RegData31), .clk(Clock));  // open: clr
  Multiplexer #(.select(5), .width(32), .enable("false")) multiplexer_1 (
    .in0({32{1'b0}}), .in1(RegData1), .in2(RegData2), .in3(RegData3), .in4(RegData4), .in5(RegData5),
    .in6(RegData6), .in7(RegData7), .in8(RegData8), .in9(RegData9), .in10(RegData10), .in11(RegData11),
    .in12(RegData12), .in13(RegData13), .in14(RegData14), .in15(RegData15), .in16(RegData16),
    .in17(RegData17), .in18(RegData18), .in19(RegData19), .in20(RegData20), .in21(RegData21),
    .in22(RegData22), .in23(RegData23), .in24(RegData24), .in25(RegData25), .in26(RegData26),
    .in27(RegData27), .in28(RegData28), .in29(RegData29), .in30(RegData30), .in31(RegData31), .out(RdData1),
    .sel(RdAddr1));
  Multiplexer #(.select(5), .width(32), .enable("false")) multiplexer_2 (
    .in0({32{1'b0}}), .in1(RegData1), .in2(RegData2), .in3(RegData3), .in4(RegData4), .in5(RegData5),
    .in6(RegData6), .in7(RegData7), .in8(RegData8), .in9(RegData9), .in10(RegData10), .in11(RegData11),
    .in12(RegData12), .in13(RegData13), .in14(RegData14), .in15(RegData15), .in16(RegData16),
    .in17(RegData17), .in18(RegData18), .in19(RegData19), .in20(RegData20), .in21(RegData21),
    .in22(RegData22), .in23(RegData23), .in24(RegData24), .in25(RegData25), .in26(RegData26),
    .in27(RegData27), .in28(RegData28), .in29(RegData29), .in30(RegData30), .in31(RegData31), .out(RdData2),
    .sel(RdAddr2));
endmodule

module Overflow (
  input  Add,
  input  Sub,
  input  ASign,
  input  BSign,
  input  ResultSign,
  output Overflow
);

  wire and_1_out, and_2_out, or_1_out, xnor_1_out, xor_1_out, xor_2_out;

  xnor xnor_1 (xnor_1_out, ASign, BSign);
  xor xor_1 (xor_1_out, ASign, BSign);
  and and_1 (and_1_out, xnor_1_out, Add);
  and and_2 (and_2_out, xor_1_out, Sub);
  or or_1 (or_1_out, and_1_out, and_2_out);
  xor xor_2 (xor_2_out, ResultSign, ASign);
  and and_3 (Overflow, or_1_out, xor_2_out);

  // Notes on the sheet:
  //   Overflow occurs when doing addition and sign(A) == sign(B) && sign(result) != sign(A)
  //   Or
  //   Overflow occurs when doing subtraction and sign(A) != sign(B) && sign(result) != sign(A)
endmodule

module _26to32 (
  input  [25:0] in_1,
  output [31:0] out_2
);


  assign out_2 = {{6{1'b0}}, in_1};
endmodule

module _16to32SE (
  input  [15:0] in_1,
  output [31:0] out_2
);

  and and_1 (out_2[31], in_1[15], 1'b1);

  assign out_2[30:0] = {{15{out_2[31]}}, in_1};
endmodule

module Control (
  input  [3:0] Current_State,
  output PCWriteCond,
  output PCWrite,
  output IorD,
  output MemRead,
  output MemWrite,
  output MemtoReg0,
  output MemtoReg1,
  output IRWrite,
  output PCSource0,
  output PCSource1,
  output ALUOp0,
  output ALUOp1,
  output ALUSrcB0,
  output ALUSrcB1,
  output ALUSrcA,
  output [2:0] NextStateSrc,
  output RegWrite,
  output RegDst0,
  output RegDst1
);

  ROM #(.addrWidth(4), .dataWidth(21)) rom_1 (
    .addr(Current_State),
    .data({NextStateSrc, RegDst1, RegDst0, RegWrite, ALUSrcA, ALUSrcB1, ALUSrcB0, ALUOp1, ALUOp0, PCSource1, PCSource0, IRWrite, MemtoReg1, MemtoReg0, MemWrite, MemRead, IorD, PCWrite, PCWriteCond}));  // open: sel

  // Notes on the sheet:
  //   contents of rom_1 (hex, n*v repeats v):
  //   108a 43000 86000 c 1c8020 1c0014 4800 1d8000 1c4501 1c0202 6c00 1c8000 28040 1c0202 1c0302 c0000
endmodule

module ALUControl (
  input  [1:0] ALUOp,
  input  [5:0] func,
  input  [5:0] op,
  output [3:0] ALUCtrl
);

  wire [3:0] rom_1_data, rom_2_data;

  ROM #(.addrWidth(6), .dataWidth(4)) rom_1 (.addr(func), .data(rom_1_data));  // open: sel
  ROM #(.addrWidth(6), .dataWidth(4)) rom_2 (.addr(op), .data(rom_2_data));  // open: sel
  Multiplexer #(.select(2), .width(4)) multiplexer_1 (
    .in0(4'b0011), .in1(4'b0100), .in2(rom_1_data), .in3(rom_2_data), .out(ALUCtrl), .sel(ALUOp));  // open: en

  // Notes on the sheet:
  //   contents of rom_1 (hex, n*v repeats v):
  //   f 0 e 29*0 3 0 4 0 6 0 5 0 0 0 2 1
  //   contents of rom_2 (hex, n*v repeats v):
  //   4*0 4 0 0 0 3 0 0 0 6 22*0 3 7*0 3
endmodule

module DispatchROM1 (
  input  [5:0] op,
  output [3:0] NextState
);

  ROM #(.addrWidth(6), .dataWidth(4)) rom_1 (.addr(op), .data(NextState));  // open: sel

  // Notes on the sheet:
  //   contents of rom_1 (hex, n*v repeats v):
  //   f 0 9 c 8 0 0 0 a 0 0 0 a a 21*0 2 7*0 2
endmodule

module DispatchROM2 (
  input  [5:0] op,
  output [3:0] NextState
);

  ROM #(.addrWidth(6), .dataWidth(4)) rom_1 (.addr(op), .data(NextState));  // open: sel

  // Notes on the sheet:
  //   contents of rom_1 (hex, n*v repeats v):
  //   35*0 3 7*0 5
endmodule

module DispatchROM3 (
  input  [5:0] func,
  output [3:0] NextState
);

  ROM #(.addrWidth(6), .dataWidth(4)) rom_1 (.addr(func), .data(NextState));  // open: sel

  // Notes on the sheet:
  //   contents of rom_1 (hex, n*v repeats v):
  //   8*6 e 55*6
endmodule

module DispatchROM4 (
  input  [2:0] in,
  output PCEnable
);

  ROM #(.addrWidth(3), .dataWidth(1)) rom_1 (.addr(in), .data(PCEnable));  // open: sel

  // Notes on the sheet:
  //   contents of rom_1 (hex, n*v repeats v):
  //   0 0 0 5*1
endmodule
